# Fritzing sketch ir-sender-sketch (saved by Fritzing 0.9.4)
breadboards: 1

parts:
  WeMos_D1_Mini1 = WeMos D1 Mini
  Q1 = NPN-Transistor [package="TO92 [THT]"]
  LED2 = LED - 5mm [color="Infrared (940nm)" package="5 mm [THT]"]

nets:
  N1: WeMos_D1_Mini1.5V, LED2.anode
  N2: WeMos_D1_Mini1.D1, Q1.B
  N3: WeMos_D1_Mini1.G, Q1.E
  N4: Q1.C, LED2.cathode
